# Fritzing sketch rpi (saved by Fritzing 0.9.3b)
breadboards: 1

parts:
  MCU1 = Raspberry Pi Zero
  LED1 = LED - 5mm [color="Red (633nm)" package="5 mm [THT]"]
  R1 = Resistor [tolerance=±5% resistance=360 package=THT]
  R2 = Resistor [tolerance=±5% resistance=360 package=THT]
  LED2 = LED - 5mm [color="Green (570nm)" package="5 mm [THT]"]

nets:
  N1: MCU1.pin_1, MCU1.pin_17
  N2: MCU1.pin_2, MCU1.pin_4
  N3: MCU1.pin_6, MCU1.pin_9, MCU1.pin_14, MCU1.pin_20, MCU1.pin_25, MCU1.pin_30, MCU1.pin_34, MCU1.pin_39, R1.Pin_1, R2.Pin_1
  N4: MCU1.pin_36, LED2.anode
  N5: MCU1.pin_38, LED1.anode
  N6: LED1.cathode, R1.Pin_0
  N7: R2.Pin_0, LED2.cathode
